# Fritzing sketch File2 (saved by Fritzing 0.9.4)
breadboards: 1

parts:
  Part1 = Arduino Uno (Rev3)
  R1 = Resistor [tolerance=±5% resistance=220 package=THT]
  R2 = Resistor [tolerance=±5% resistance=220 package=THT]
  LED1 = LED - 5mm [color="Red (633nm)" package="5 mm [THT]"]
  S1 = Pushbutton [package="[THT]"]

nets:
  N1: Part1.D8, R2.Pin_0, S1.Pin_1, S1.Pin_2
  N2: Part1.GND, R1.Pin_0, R2.Pin_1
  N3: Part1.D2, LED1.anode
  N4: Part1.3V3, S1.Pin_3, S1.Pin_4
  N5: R1.Pin_1, LED1.cathode
