# Fritzing sketch file1 (saved by Fritzing 0.9.4)
breadboards: 1

parts:
  Part2 = Arduino Uno (Rev3)
  LED1 = smd LED [color="Red (633nm)" package="0603 [SMD]"]  # not connected
  R1 = Resistor [tolerance=±5% resistance=220 package=THT]

nets:
  N1: Part2.GND, R1.Pin_1
